// Logisim project Lab4DataPatht5newReg.circ as structural Verilog: 6 circuits, main circuit main
module main (
  input  [2:0] F,
  input  [31:0] A,
  input  [31:0] B,
  input  in_4,
  input  [2:0] A1,
  input  [2:0] A2,
  input  [2:0] A3,
  input  [31:0] WD3,
  output Zero,
  output [31:0] Y,
  output [31:0] R1,
  output [31:0] R2,
  output [31:0] T2
);

  wire button_1_out;

  Button button_1 (.out(button_1_out));
  // ALU alu_1: pin names not known; wires that end beside it: A, B, F, Zero, Y
  RegisterFile registerfile_1 (
    .CLK(button_1_out), .A1(A1), .WD3(WD3), .A2(A2), .WE3(in_4), .RD1(R1), .RD2(R2), .A3(A3), .T2(T2));  // open: out_7, T0, T1, RA, TP

  // Notes on the sheet:
  //   000 = +
  //   001 = -
  //   010 = AND
  //   011 = OR
  //   101 = A < B
endmodule

module ALU (
  input  [2:0] F,
  input  [31:0] B,
  input  [31:0] A,
  output ZeroNAND,
  output Zero,
  output [31:0] Y
);

  wire [0:0] comparator_1_lt;
  wire [31:0] adder_1_out, and_1_out, multiplexer_1_out, not_1_out, or_1_out;
  wire [31:1] nand_1_out;

  assign not_1_out = ~B;  // NOT_Gate not_1, 32 bits wide
  Multiplexer #(.width(32), .enable("false")) multiplexer_1 (
    .in0(B), .in1(not_1_out), .out(multiplexer_1_out), .sel(F[0]));
  Adder #(.width(32)) adder_1 (.a(multiplexer_1_out), .b(A), .out(adder_1_out), .cin(F[0]));  // open: cout
  assign and_1_out = B & A;  // AND_Gate and_1, 32 bits wide
  assign or_1_out = B | A;  // OR_Gate or_1, 32 bits wide
  Comparator #(.width(32), .mode("unsigned")) comparator_1 (.a(A), .b(B), .lt(comparator_1_lt[0]));  // open: gt, eq
  Multiplexer #(.select(3), .width(32), .enable("false")) multiplexer_2 (
    .in0(adder_1_out), .in1(adder_1_out), .in2(and_1_out), .in3(or_1_out),
    .in5({{31{1'b0}}, comparator_1_lt[0]}), .out(Y), .sel(F));  // open: in4, in6, in7
  assign {nand_1_out, ZeroNAND} = ~(Y & {32{1'b0}});  // NAND_Gate nand_1, 32 bits wide
  Comparator #(.width(32), .mode("unsigned")) comparator_2 (.a(Y), .b({32{1'b0}}), .eq(Zero));  // open: gt, lt
endmodule

module Datapath (
  output [31:0] R1,
  output [31:0] R2,
  output [31:0] Y,
  output [31:0] t2,
  output [31:0] t1,
  output [7:0] _8bit_b_type_imm__non_0_bit,
  output [7:0] _8bit_b_type_imm__w_0_bit,
  output [31:0] t0,
  output [11:0] t0_2,
  output [31:0] tp,
  output [31:0] ra
);

  wire alu_1_p4, and_1_out, button_1_out, clock_1_out, controlunit_1_alusrc, controlunit_1_branch,
       controlunit_1_regwrite;
  wire [2:0] controlunit_1_alucontrol;
  wire [7:0] adder_1_out, adder_2_out, multiplexer_1_out, register_1_q, shifter_1_out;
  wire [24:0] rom_1_data;
  wire [31:0] bit_extender_1_out, multiplexer_2_out;

  Clock clock_1 (.out(clock_1_out));
  Multiplexer #(.width(8), .enable("false")) multiplexer_1 (
    .in0(adder_1_out), .in1(adder_2_out), .out(multiplexer_1_out), .sel(and_1_out));
  Button button_1 (.out(button_1_out));
  Register register_1 (.D(multiplexer_1_out), .Q(register_1_q), .clk(clock_1_out), .clr(button_1_out));  // open: en
  Adder adder_1 (.a(register_1_q), .b(8'h4), .out(adder_1_out));  // open: cin, cout
  Shifter #(.shift("lr")) shifter_1 (.in(register_1_q), .\dist (3'b010), .out(shifter_1_out));
  ROM #(.dataWidth(32)) rom_1 (
    .addr(shifter_1_out),
    .data({t0_2[11], t0_2[9:8], _8bit_b_type_imm__non_0_bit[7:4], rom_1_data[24:12], _8bit_b_type_imm__non_0_bit[3:0], t0_2[10], rom_1_data[6:0]}));  // open: sel
  RegisterFile registerfile_1 (
    .CLK(clock_1_out), .A1(rom_1_data[17:15]), .WD3(Y), .A2(rom_1_data[22:20]), .WE3(controlunit_1_regwrite),
    .RD1(R1), .RD2(R2), .A3({_8bit_b_type_imm__non_0_bit[1:0], t0_2[10]}), .T2(t2), .T0(t0), .T1(t1),
    .RA(ra), .TP(tp));  // open: out_7
  assign bit_extender_1_out = {{20{t0_2[11]}}, {t0_2[11], t0_2[9:8], _8bit_b_type_imm__non_0_bit[7:4], rom_1_data[24:20]}};  // Bit_Extender bit_extender_1
  ControlUnit controlunit_1 (
    .RegWrite(controlunit_1_regwrite), .ALUSrc(controlunit_1_alusrc), .ALUControl(controlunit_1_alucontrol),
    .Branch(controlunit_1_branch),
    .Instruction({t0_2[11], t0_2[9:8], _8bit_b_type_imm__non_0_bit[7:4], rom_1_data[24:12], _8bit_b_type_imm__non_0_bit[3:0], t0_2[10], rom_1_data[6:0]}));
  Multiplexer #(.width(32), .enable("false")) multiplexer_2 (
    .in0(R2), .in1(bit_extender_1_out), .out(multiplexer_2_out), .sel(controlunit_1_alusrc));
  // ALU alu_1: pin names not known; wires that end beside it: R1, multiplexer_2_out, controlunit_1_alucontrol, alu_1_p4, Y
  Adder adder_2 (.a(register_1_q), .b(_8bit_b_type_imm__w_0_bit), .out(adder_2_out));  // open: cin, cout
  Shifter shifter_2 (.in(_8bit_b_type_imm__non_0_bit), .\dist (3'b001), .out(_8bit_b_type_imm__w_0_bit));
  and and_1 (and_1_out, controlunit_1_branch, alu_1_p4);

  assign t0_2[7:0] = _8bit_b_type_imm__non_0_bit;

  // Notes on the sheet:
  //   PC
  //   contents of rom_1 (hex, n*v repeats v):
  //   400293 100393 28233 b3 fff28313 2728c63 2028a63 2000063 fff20213 2020463 82b3 83b3 b3 fff20313 263
  //   fe0302e3 5080b3 fff30313 fe000ae3 63
  //   b-type Imm
endmodule

// T0
module RegisterFile (
  input  CLK,
  input  [2:0] A1,
  input  [31:0] WD3,
  input  [2:0] A2,
  input  WE3,
  input  [2:0] A3,
  output out_7,
  output [31:0] RD1,
  output [31:0] RD2,
  output [31:0] T2,
  output [31:0] T1,
  output [31:0] T0,
  output [31:0] RA,
  output [31:0] TP
);

  wire and_1_out, and_2_out, and_3_out, and_4_out, and_5_out, and_6_out, and_7_out, decoder_1_out1,
       decoder_1_out2, decoder_1_out3, decoder_1_out4, decoder_1_out5, decoder_1_out6, decoder_1_out7;
  wire [31:0] gp_q, sp_q, Zero_q;

  Decoder #(.select(3), .enable("false")) decoder_1 (
    .out0(out_7), .out1(decoder_1_out1), .out2(decoder_1_out2), .out3(decoder_1_out3), .out4(decoder_1_out4),
    .out5(decoder_1_out5), .out6(decoder_1_out6), .out7(decoder_1_out7), .sel(A3));
  and and_1 (and_1_out, WE3, decoder_1_out1);
  and and_2 (and_2_out, WE3, decoder_1_out2);
  and and_3 (and_3_out, WE3, decoder_1_out3);
  and and_4 (and_4_out, WE3, decoder_1_out4);
  and and_5 (and_5_out, WE3, decoder_1_out5);
  and and_6 (and_6_out, WE3, decoder_1_out6);
  and and_7 (and_7_out, WE3, decoder_1_out7);
  Register #(.width(32)) Zero (.Q(Zero_q));  // open: D, en, clk, clr
  Register #(.width(32)) u_ra (.D(WD3), .en(and_1_out), .Q(RA), .clk(CLK));  // open: clr
  Register #(.width(32)) sp (.D(WD3), .en(and_2_out), .Q(sp_q), .clk(CLK));  // open: clr
  Register #(.width(32)) gp (.D(WD3), .en(and_3_out), .Q(gp_q), .clk(CLK));  // open: clr
  Register #(.width(32)) u_tp (.D(WD3), .en(and_4_out), .Q(TP), .clk(CLK));  // open: clr
  Register #(.width(32)) u_t0 (.D(WD3), .en(and_5_out), .Q(T0), .clk(CLK));  // open: clr
  Register #(.width(32)) u_t1 (.D(WD3), .en(and_6_out), .Q(T1), .clk(CLK));  // open: clr
  Register #(.width(32)) u_t2 (.D(WD3), .en(and_7_out), .Q(T2), .clk(CLK));  // open: clr
  Multiplexer #(.select(3), .width(32), .enable("false")) multiplexer_1 (
    .in0(Zero_q), .in1(RA), .in2(sp_q), .in3(gp_q), .in4(TP), .in5(T0), .in6(T1), .in7(T2), .out(RD1),
    .sel(A1));
  Multiplexer #(.select(3), .width(32), .enable("false")) multiplexer_2 (
    .in0(Zero_q), .in1(RA), .in2(sp_q), .in3(gp_q), .in4(TP), .in5(T0), .in6(T1), .in7(T2), .out(RD2),
    .sel(A2));
endmodule

module ControlUnit (
  input  [31:0] Instruction,
  output RegWrite,
  output ALUSrc,
  output [2:0] ALUControl,
  output Branch
);

  wire alu_1_p4, and_1_out, comparator_1_eq, comparator_3_eq;
  wire [2:0] bit_extender_1_out;
  wire [31:0] registerfile_1_rd1, registerfile_1_rd2;

  Comparator #(.width(7), .mode("unsigned")) comparator_1 (
    .a(Instruction[6:0]), .b(7'b1100011), .eq(comparator_1_eq));  // open: gt, lt
  Comparator #(.width(7), .mode("unsigned")) comparator_2 (
    .a(Instruction[6:0]), .b(7'b0010011), .eq(ALUSrc));  // open: gt, lt
  Comparator #(.width(7), .mode("unsigned")) comparator_3 (
    .a(Instruction[6:0]), .b(7'b0110011), .eq(comparator_3_eq));  // open: gt, lt
  RegisterFile registerfile_1 (
    .A1(Instruction[17:15]), .A2(Instruction[22:20]), .RD1(registerfile_1_rd1), .RD2(registerfile_1_rd2));  // open: CLK, WD3, WE3, A3, T2, out_7, T0, T1, RA, TP
  and and_1 (and_1_out, comparator_3_eq, Instruction[25]);
  // ALU alu_1: pin names not known; wires that end beside it: registerfile_1_rd1, registerfile_1_rd2, ALUControl, alu_1_p4
  or or_1 (RegWrite, ALUSrc, comparator_3_eq);
  and and_2 (Branch, comparator_1_eq, alu_1_p4);
  assign bit_extender_1_out = {{2{1'b0}}, comparator_1_eq};  // Bit_Extender bit_extender_1
  Multiplexer #(.width(3), .enable("false")) multiplexer_1 (
    .in0(bit_extender_1_out), .in1(3'b100), .out(ALUControl), .sel(and_1_out));

  // Notes on the sheet:
  //   25
  //   Beq
  //   Addi
  //   Add
  //   Mul
endmodule

module Tests (
  output [31:0] Y,
  output [3:0] Y_2,
  output [7:0] Y_3
);


  assign Y = 32'hf4010207;
  assign Y_2 = 4'b0010;
  assign Y_3 = 8'h22;

  // Notes on the sheet:
  //   binary values in Logisim. Convince yourself how the bits are displayed.
  //   Example 1: A simple example that illustrates how 32-bit values are displayed as 
  //   Example 2) An example of how to extra certain bits from a (in this case) 32-bit wire. Here we extract the bits 8..11 from the 32-bit wire.
  //   Example 3) Sometimes it is useful to extra bits from different position and the re-assemble them. In this case, we extract bits 8..11 and bits 15..18 and assemble them into an 8-bit wire.
endmodule
